// Logisim project SR Flip Flop (Active High).circ as structural Verilog: 1 circuit, main circuit main
module main (
  input  Set,
  input  Reset,
  output out_3,
  output out_4
);

  wire and_1_out, and_2_out, clock_1_out;

  Clock clock_1 (.out(clock_1_out));
  and and_1 (and_1_out, Set, clock_1_out);
  and and_2 (and_2_out, clock_1_out, Reset);
  nor nor_1 (out_3, and_1_out, out_4);
  nor nor_2 (out_4, out_3, and_2_out);
endmodule
